# Fritzing sketch schematic (saved by Fritzing 1.0.4)

parts:
  Mod1 = Amica NodeMCU DEVKIT 1.0
  M2 = CK-07 [package=THT]
  Bauteil1 = FC-28 Soil Hygrometer Module - Probe
  HC-SR04_Sensor_1 = HC-SR04 Ultrasonic Distance Sensor
  SERVO1 = Tower Pro SG90 servo [part_number=101246]
  e-radionica_com1 = LM393 LDR breakout [part_number=100027]
  DHT1 = DHT22 Humidity and Temperature Sensor
  KY-1 = Keyes Relay [package=THT]
  LCD2004-I2C1 = LCD2004-I2C

nets:
  VCC: Mod1.pin1, Mod1.pin_26, M2.pin_4, HC-SR04_Sensor_1.VCC, e-radionica_com1.VCC, DHT1.VDD
  GND: Mod1.pin2, Mod1.pin_9, Mod1.pin_29, M2.pin_3, HC-SR04_Sensor_1.GND, SERVO1.GND, e-radionica_com1.GND, DHT1.GND, KY-1.ground, LCD2004-I2C1.GND
  N1: Mod1.pin6, SERVO1.Signal
  N2: Mod1.pin7, HC-SR04_Sensor_1.ECHO
  N3: Mod1.pin8, HC-SR04_Sensor_1.TRIG
  N4: Mod1.pin_11, DHT1.DATA
  N5: Mod1.pin_12, KY-1.signal
  N6: Mod1.pin_13, LCD2004-I2C1.SDA
  N7: Mod1.pin_14, LCD2004-I2C1.SCL
  N8: Mod1.pin_15, e-radionica_com1.DO
  N9: Mod1.pin_16, M2.pin_1
  +5V: Mod1.pin_30, SERVO1.+5V, KY-1.power, LCD2004-I2C1.VCC
  N10: M2.pin_5, Bauteil1.NEG
  N11: M2.pin_6, Bauteil1.POS

custom parts:
  CK-07: Fc-51 Infrared Obstacle Avoidance Proximity Sensor module. IR transmitter led, receiver LED, lm393 compaitor and a pot. 3.3 V to 5V power.
  FC-28 Soil Hygrometer Module - Probe: The FC-28 is a soil hygrometer module that uses the Texas Instruments LM393 comparator chip to provide an analog measurement of soil humidity.
  Tower Pro SG90 servo: Original file by John De Cristofaro http://www.adafruit.com/products/1449 Adafruit Feedback Servo (Small) Edited by: e-radionica.com 28/9/2015
  Keyes Relay: The Keyes 5V relay module is suitable for SCM development, home appliance control. It uses a 5V~12V TIL control signal which can control DC / AC signal.
  LCD2004-I2C: A standard character display with 4x20 characters. Comes in many colors with LCM2004 IIC attached.
